// Logisim project TópicosEspeciaisI.circ as structural Verilog: 1 circuit, main circuit main
module main (
  input  A,
  input  B,
  input  C,
  input  D,
  output out_5
);

  wire and_1_out, not_1_out, not_2_out, or_1_out;

  not not_1 (not_1_out, A);
  or or_1 (or_1_out, A, D);
  and and_1 (and_1_out, not_1_out, B, C);
  not not_2 (not_2_out, or_1_out);
  and and_2 (out_5, and_1_out, not_2_out);
endmodule
